# Fritzing sketch schema (saved by Fritzing 0.9.3b)
breadboards: 1

parts:
  Raspberry_Pi1 = Raspberry Pi B+
  IC1 = L293D [package=THT]
  M1 = DC Motor
  VCC1 = 4 x AAA Battery Mount

nets:
  N1: Raspberry_Pi1.GPIO25, IC1.Enable_1
  N2: Raspberry_Pi1.GPIO24, Raspberry_Pi1.GPIO18, IC1.In_2
  N3: Raspberry_Pi1.GPIO23, Raspberry_Pi1.GPIO15, IC1.In_1
  N4: Raspberry_Pi1.GND, IC1.0V, VCC1.-
  N5: Raspberry_Pi1.5V, IC1.+V
  N6: IC1.Out_1_(_Controlled_by_Enable_1_), M1.pin_2
  N7: IC1.Out_2_(_Controlled_by_Enable_1_), M1.pin_1
  N8: IC1.+Vmotor, VCC1.+
